// Logisim project 2 bit counter.circ as structural Verilog: 2 circuits, main circuit main
module main (
  output Q1
);

  wire clock_1_out, t_ff_1_q;

  Clock clock_1 (.out(clock_1_out));
  T_Flip_Flop t_ff_1 (.clk(1'b1), .Q(t_ff_1_q));  // open: T, Qn, preset, reset, en
  T_Flip_Flop t_ff_2 (.clk(t_ff_1_q), .Q(Q1));  // open: T, Qn, preset, reset, en
endmodule

module _3bit (
  output Q2,
  output Q1,
  output Q0
);

  wire and_1_out, clock_1_out;

  Clock clock_1 (.out(clock_1_out));
  T_Flip_Flop T0 (.clk(clock_1_out), .T(1'b1), .Q(Q0));  // open: Qn, preset, reset, en
  T_Flip_Flop T1 (.clk(clock_1_out), .Q(Q1));  // open: T, Qn, preset, reset, en
  and and_1 (and_1_out, Q1, Q0);
  T_Flip_Flop T2 (.clk(clock_1_out), .T(and_1_out), .Q(Q2));  // open: Qn, preset, reset, en
endmodule
