// Logisim project ExitQuiz15.circ as structural Verilog: 1 circuit, main circuit main
module main (
);

  wire and_1_out, clock_1_out, not_1_out, not_2_out, T0_q, T1_q;

  Clock clock_1 (.out(clock_1_out));
  T_Flip_Flop T0 (.clk(clock_1_out), .T(1'b1), .Q(T0_q));  // open: Qn, preset, reset, en
  T_Flip_Flop T1 (.clk(clock_1_out), .T(T0_q), .Q(T1_q));  // open: Qn, preset, reset, en
  not not_1 (not_1_out, T0_q);
  not not_2 (not_2_out, T1_q);
  LED Q1_prime (.in(not_2_out));
  LED Q0 (.in(T0_q));
  LED Q0_prime_Q1 (.in(and_1_out));
  and and_1 (and_1_out, not_1_out, T1_q);
endmodule
