// Logisim project QUIZ11Circuit.circ as structural Verilog: 1 circuit, main circuit main
module main (
  input  R,
  input  S,
  output out_3,
  output out_4
);

  nand nand_1 (out_3, R, out_4);
  nand nand_2 (out_4, out_3, S);
endmodule
