// Logisim project SP2.circ as structural Verilog: 1 circuit, main circuit main
module main (
);

  wire and_1_out, and_2_out, and_3_out, clock_1_out, not_1_out, or_1_out, t_ff_1_q, t_ff_1_qn, t_ff_2_q,
       t_ff_2_qn, Walk_Button_out;

  Clock clock_1 (.out(clock_1_out));
  Button Walk_Button (.out(Walk_Button_out));
  T_Flip_Flop t_ff_1 (.clk(clock_1_out), .T(t_ff_2_q), .Q(t_ff_1_q), .Qn(t_ff_1_qn), .reset(1'b0));  // open: preset, en
  T_Flip_Flop t_ff_2 (.clk(clock_1_out), .T(or_1_out), .Q(t_ff_2_q), .Qn(t_ff_2_qn), .reset(1'b0));  // open: preset, en
  or or_1 (or_1_out, t_ff_2_q, Walk_Button_out, t_ff_1_q);
  and and_1 (and_1_out, t_ff_2_q, t_ff_1_qn);
  and and_2 (and_2_out, t_ff_2_qn, t_ff_1_qn);
  and and_3 (and_3_out, t_ff_2_qn, t_ff_1_q);
  not not_1 (not_1_out, and_3_out);
  LED Red (.in(t_ff_1_q));
  LED Yellow (.in(and_1_out));
  LED Green (.in(and_2_out));
  LED Walk (.in(and_3_out));
  LED Stop (.in(not_1_out));
endmodule
