// Logisim project Segments.circ as structural Verilog
module d (
  input  A,
  input  B,
  output out_3
);

  wire not_1_out, not_2_out;

  not not_1 (not_1_out, A);
  not not_2 (not_2_out, B);
  or or_1 (out_3, not_1_out, not_2_out);
endmodule

module f (
  input  A,
  input  B,
  output out_3
);

  wire not_1_out;

  not not_1 (not_1_out, A);
  or or_1 (out_3, not_1_out, B);
endmodule

module g (
  input  B_prime,
  input  C,
  input  C_2,
  input  D_prime,
  input  A,
  input  B_prime_2,
  input  A_2,
  input  D,
  input  A_prime,
  input  B,
  input  C_3,
  output out_12
);

  wire and_1_out, and_2_out, and_3_out, and_4_out, and_5_out;

  and and_1 (and_1_out, B_prime, C);
  and and_2 (and_2_out, C_2, D_prime);
  and and_3 (and_3_out, A, B_prime_2);
  and and_4 (and_4_out, A_2, D);
  and and_5 (and_5_out, A_prime, B, C_3);
  or or_1 (out_12, and_1_out, and_2_out, and_3_out, and_4_out, and_5_out);
endmodule

module a (
  input  A,
  input  A_prime,
  input  B,
  input  B_prime,
  input  C,
  input  C_prime,
  input  D,
  input  D_prime,
  output out_9
);

  wire and_1_out, and_2_out, and_3_out, and_4_out, and_5_out;

  and and_1 (and_1_out, B_prime, C);
  and and_2 (and_2_out, C, D_prime);
  and and_3 (and_3_out, A, B_prime);
  and and_4 (and_4_out, A, D);
  and and_5 (and_5_out, A_prime, B, C_prime);
  or or_1 (out_9, and_1_out, and_2_out, and_3_out, and_4_out, and_5_out);
endmodule
