// Logisim project TakeHomeExam.circ as structural Verilog: 1 circuit, main circuit main
module main (
  input  s1,
  input  s0,
  input  in_3,
  input  in_4,
  output A,
  output B,
  output C,
  output D,
  output E,
  output F,
  output G
);

  or or_1 (C, s0, s1);
  not not_1 (E, s0);
  or or_2 (G, s0, s1);
  Decoder decoder_1 ();  // open: out0, out1, sel, en
  _7_Segment_Display u_7_segment_display_1 (.g(G), .f(1'b1), .a(1'b1), .b(in_3), .e(E), .d(1'b1), .c(C), .dp(in_4));

  assign A = 1'b1;
  assign B = in_3;
  assign D = 1'b1;
  assign F = 1'b1;
endmodule
