// Logisim project exitquiz14.circ as structural Verilog: 1 circuit, main circuit main
module main (
);

  wire clock_1_out, clock_2_out, clock_3_out, t_ff_1_q, t_ff_2_q, t_ff_3_q, xor_1_out;

  xor xor_1 (xor_1_out, t_ff_3_q, t_ff_2_q);
  Clock clock_1 (.out(clock_1_out));
  Clock clock_2 (.out(clock_2_out));
  Clock clock_3 (.out(clock_3_out));
  T_Flip_Flop t_ff_1 (.clk(xor_1_out), .T(clock_1_out), .Q(t_ff_1_q));  // open: Qn, preset, reset, en
  T_Flip_Flop t_ff_2 (.clk(1'b1), .T(clock_2_out), .Q(t_ff_2_q));  // open: Qn, preset, reset, en
  T_Flip_Flop t_ff_3 (.T(clock_3_out), .Q(t_ff_3_q));  // open: clk, Qn, preset, reset, en
endmodule
