// Logisim project exitquiz16.circ as structural Verilog: 2 circuits, main circuit 1-Bit ALU
module _1_Bit_ALU (
  input  Borrow_in,
  input  Carry_in,
  input  A,
  input  B,
  input  [1:0] Sel,
  output Cout,
  output F,
  output Bout
);

  wire adder_1_out, and_1_out, or_1_out, subtractor_1_out;

  Adder #(.width(1)) adder_1 (.a(A), .b(B), .out(adder_1_out), .cin(Carry_in), .cout(Cout));
  Subtractor #(.width(1)) subtractor_1 (.a(A), .b(B), .out(subtractor_1_out), .bin(Borrow_in), .bout(Bout));
  and and_1 (and_1_out, A, B);
  or or_1 (or_1_out, A, B);
  Multiplexer #(.select(2), .enable("false")) multiplexer_1 (
    .in0(adder_1_out), .in1(subtractor_1_out), .in2(and_1_out), .in3(or_1_out), .out(F), .sel(Sel));
endmodule

module _4_bit_ALU (
  input  Borrow_in,
  input  Carry_in,
  input  A0,
  input  B0,
  input  A1,
  input  B1,
  input  A2,
  input  B2,
  input  A3,
  input  B3,
  input  [1:0] Op_Sel,
  output F0,
  output F1,
  output F2,
  output F3,
  output Bout,
  output Cout
);

  wire _1_Bit_ALU_2_bout, _1_Bit_ALU_2_cout, _1_Bit_ALU_3_bout, _1_Bit_ALU_3_cout, _1_Bit_ALU_bout,
       _1_Bit_ALU_cout;

  _1_Bit_ALU _1_Bit_ALU (
    .Borrow_in(Borrow_in), .Carry_in(Carry_in), .A(A0), .B(B0), .Sel(Op_Sel), .Cout(_1_Bit_ALU_cout), .F(F0),
    .Bout(_1_Bit_ALU_bout));
  _1_Bit_ALU _1_Bit_ALU_2 (
    .Borrow_in(_1_Bit_ALU_bout), .Carry_in(_1_Bit_ALU_cout), .A(A1), .B(B1), .Sel(Op_Sel),
    .Cout(_1_Bit_ALU_2_cout), .F(F1), .Bout(_1_Bit_ALU_2_bout));
  _1_Bit_ALU _1_Bit_ALU_3 (
    .Borrow_in(_1_Bit_ALU_2_bout), .Carry_in(_1_Bit_ALU_2_cout), .A(A2), .B(B2), .Sel(Op_Sel),
    .Cout(_1_Bit_ALU_3_cout), .F(F2), .Bout(_1_Bit_ALU_3_bout));
  _1_Bit_ALU _1_Bit_ALU_4 (
    .Borrow_in(_1_Bit_ALU_3_bout), .Carry_in(_1_Bit_ALU_3_cout), .A(A3), .B(B3), .Sel(Op_Sel), .Cout(Cout),
    .F(F3), .Bout(Bout));
endmodule
