// Logisim project synchronous 2 bit counter.circ as structural Verilog: 1 circuit, main circuit main
module main (
  output Q1,
  output Q1_2
);

  wire and_1_out, and_2_out, and_3_out, and_4_out, clock_1_out, clock_2_out, clock_3_out, clock_4_out,
       clock_5_out, clock_6_out, clock_7_out, clock_8_out, d_ff_1_q, d_ff_2_q, d_ff_3_q, d_ff_4_qn, d_ff_5_q,
       d_ff_5_qn, d_ff_6_q, j_k_ff_1_q, not_1_out, or_1_out, or_2_out, t_ff_1_q;

  Clock clock_1 (.out(clock_1_out));
  Clock clock_2 (.out(clock_2_out));
  T_Flip_Flop t_ff_1 (.clk(1'b1), .Q(t_ff_1_q));  // open: T, Qn, preset, reset, en
  J_K_Flip_Flop j_k_ff_1 (.J(1'b1), .clk(clock_2_out), .Q(j_k_ff_1_q));  // open: K, Qn, preset, en, reset
  T_Flip_Flop t_ff_2 (.clk(t_ff_1_q), .Q(Q1));  // open: T, Qn, preset, reset, en
  J_K_Flip_Flop j_k_ff_2 (.J(j_k_ff_1_q), .clk(clock_2_out), .Q(Q1_2));  // open: K, Qn, preset, en, reset
  not not_1 (not_1_out, d_ff_2_q);
  or or_1 (or_1_out, d_ff_1_q, d_ff_2_q);
  D_Flip_Flop d_ff_1 (.clk(not_1_out), .D(clock_3_out), .Q(d_ff_1_q));  // open: Qn, preset, en, reset
  Clock clock_3 (.out(clock_3_out));
  D_Flip_Flop d_ff_2 (.clk(or_1_out), .D(clock_4_out), .Q(d_ff_2_q));  // open: Qn, preset, en, reset
  Clock clock_4 (.out(clock_4_out));
  D_Flip_Flop d_ff_3 (.clk(d_ff_2_q), .D(clock_5_out), .Q(d_ff_3_q));  // open: Qn, preset, en, reset
  Clock clock_5 (.out(clock_5_out));
  Clock clock_6 (.out(clock_6_out));
  Clock clock_7 (.out(clock_7_out));
  Clock clock_8 (.out(clock_8_out));
  D_Flip_Flop d_ff_4 (.clk(and_1_out), .D(clock_6_out), .Qn(d_ff_4_qn));  // open: Q, preset, en, reset
  D_Flip_Flop d_ff_5 (.clk(and_2_out), .D(clock_7_out), .Q(d_ff_5_q), .Qn(d_ff_5_qn));  // open: preset, en, reset
  D_Flip_Flop d_ff_6 (.clk(or_2_out), .D(clock_8_out), .Q(d_ff_6_q));  // open: Qn, preset, en, reset
  and and_1 (and_1_out, d_ff_4_qn, d_ff_5_q, d_ff_6_q);
  and and_2 (and_2_out, d_ff_4_qn, d_ff_5_qn, d_ff_6_q);
  and and_3 (and_3_out, d_ff_4_qn, d_ff_5_qn);
  or or_2 (or_2_out, and_3_out, and_4_out);
  and and_4 (and_4_out, d_ff_4_qn, d_ff_6_q);
endmodule
